# Fritzing sketch Schema_DL002A (saved by Fritzing 0.8.3b)
breadboards: 1

parts:
  Componente1 = Arduino Uno (Rev3)
  kEYPAD_MATRICIAL_1 = KEYPAD 4x3
  J1 = Piezo Speaker
  K1 = Relay [part_number=FRS1B-S package=THT]
  S1 = Toggle Switch [package=THT]
  TRS1 = Audio Jack (TRS) 3.5mm [package="4Ucon 08780 [THT]"]
  S2 = Round Pushbutton
  R4 = Resistor [tolerance=±5% resistance=10k package=THT]
  R5 = Resistor [tolerance=±5% resistance=330 package=THT]
  S3 = Toggle Switch [package=THT]
  D1 = LED_BARGRAPH_10 [package=led_bargaph_10]
  U2 = 7-SEGMENT-4DIGIT [package=7-segment-4digit]

nets:
  N1: Componente1.A0, kEYPAD_MATRICIAL_1.col1
  N2: Componente1.A1, kEYPAD_MATRICIAL_1.arrow1
  N3: Componente1.A2, kEYPAD_MATRICIAL_1.col2
  N4: Componente1.A3, kEYPAD_MATRICIAL_1.arrow2
  N5: Componente1.A4/SDA, kEYPAD_MATRICIAL_1.col3
  N6: Componente1.A5/SCL, kEYPAD_MATRICIAL_1.arrow3
  N7: Componente1.ICSP_MOSI, Componente1.D11_PWM/MOSI, Componente1.D12/MISO, kEYPAD_MATRICIAL_1.arrow4
  N8: Componente1.GND, J1.pin1, K1.COIL1, S1.L2, D1.F_A, U2.2, U2.3
  N9: Componente1.D8, S3.COM
  N10: Componente1.D9_PWM, R5.Pin_1
  N11: Componente1.D10_PWM/SS, K1.C1, K1.C2
  N12: Componente1.D13/SCK, R4.Pin_0
  N13: Componente1.D2, D1.D_A
  N14: Componente1.D3_PWM, D1.C_A
  N15: Componente1.D4, U2.1
  N16: Componente1.5V, K1.COIL2, S1.L1, TRS1.Sleeve, S2.leg1, D1.E_A, U2.4
  N17: J1.pin2, S3.L1, S3.L2
  N18: S1.COM, R5.Pin_0
  N19: TRS1.Ring, TRS1.Tip, S2.leg0, R4.Pin_1

notes:
  JACK mono 1/4" female for pedal
  This should be a 4x4 keypad, if only Fritzing had the model
  Grove LED Bar (serial)
  http://www.seeedstudio.com/wiki/Grove_-_LED_Bar
  wire DI to pin 2
  and DCKI to pin 3
  Sparkfun 7-Segment Serial Display
  https://www.sparkfun.com/products/11441
  Wire RX to pin 4,
  GND and VCC as usual.

custom parts:
  KEYPAD 4x3: KEYPAD matricial de 12 botones, 4 filas x 3 columnas
